# Fritzing sketch bridge_circuit (saved by Fritzing 0.9.3b)
circuit board: 7.03382cm x 5.72189cm
breadboards: 1

parts:
  Part1 = Arduino Uno (Rev3)
  J1 = Camdenboss CTB0158-2 [part_number=CTB0158-2 package=THT]
  J2 = Camdenboss CTB0158-2 [part_number=CTB0158-2 package=THT]
  U1 = LM 358 Dual Op-Amp [package="DIP8 [THT]"]

nets:
  N1: Part1.A0, J1.pin2
  N2: Part1.GND, J1.pin1, J2.pin1, U1.connector3
  N3: Part1.D5_PWM, U1.connector2
  N4: Part1.5V, U1.connector7
  N5: J2.pin2, U1.connector0, U1.connector1
