# Fritzing sketch bridge_circuit_second_order (saved by Fritzing 0.9.3b)
breadboards: 1

parts:
  Part1 = Arduino Uno (Rev3)
  R1 = Resistor [tolerance=±10% resistance=100k package=THT]
  C1 = Electrolytic Capacitor [capacitance=1µF package="100 mil [THT, electrolytic]"]
  C2 = Electrolytic Capacitor [capacitance=1µF package="100 mil [THT, electrolytic]"]
  R2 = Resistor [tolerance=±10% resistance=100k package=THT]

nets:
  N1: Part1.A0, C2.+, R2.Pin_1
  N2: Part1.D3_PWM, R1.Pin_0
  N3: Part1.GND, C1.-, C2.-
  N4: R1.Pin_1, C1.+, R2.Pin_0
